// Digital circuit control_bomba.dig as structural Verilog
module control_bomba (
  input  tanqueH,
  input  tanqueL,
  input  cisternaOK,
  input  cisternaL,
  output bomba
);

  wire not_1_out, not_2_out;

  not not_1 (not_1_out, tanqueH);
  not not_2 (not_2_out, tanqueL);
  and and_1 (bomba, not_1_out, not_2_out, cisternaOK, cisternaL);
endmodule
